// Logisim project TME1.circ as structural Verilog: 6 circuits, main circuit mon_xor
module mon_xor (
  input  a,
  input  b,
  output out_3
);

  wire and_1_out, and_2_out, not_1_out, not_2_out;

  and and_1 (and_1_out, a, not_1_out);
  not not_1 (not_1_out, b);
  not not_2 (not_2_out, a);
  and and_2 (and_2_out, not_2_out, b);
  or or_1 (out_3, and_1_out, and_2_out);
endmodule

module MUX2 (
  input  in_1,
  input  in_2,
  input  in_3,
  output out_4
);

  wire not_1_out, or_1_out, or_2_out;

  or or_1 (or_1_out, in_1, in_2);
  or or_2 (or_2_out, in_3, not_1_out);
  not not_1 (not_1_out, in_1);
  and and_1 (out_4, or_1_out, or_2_out);
endmodule

module mux2sur4bits (
  input  in_1,
  input  in_2,
  input  in_3,
  input  in_4,
  input  in_5,
  input  in_6,
  input  in_7,
  input  in_8,
  input  in_9,
  output out_10,
  output out_11,
  output out_12,
  output out_13
);

  MUX2 mux2_1 (.in_1(in_1), .in_2(in_2), .in_3(in_6), .out_4(out_10));
  MUX2 mux2_2 (.in_1(in_1), .in_2(in_3), .in_3(in_7), .out_4(out_11));
  MUX2 mux2_3 (.in_1(in_1), .in_2(in_4), .in_3(in_8), .out_4(out_12));
  MUX2 mux2_4 (.in_1(in_1), .in_2(in_5), .in_3(in_9), .out_4(out_13));
endmodule

module \mux4entrées  (
  input  in_1,
  input  in_2,
  input  in_3,
  input  in_4,
  input  in_5,
  input  in_6,
  output out_7
);

  wire mux2_1_out_4, mux2_2_out_4;

  MUX2 mux2_1 (.in_1(in_1), .in_2(in_3), .in_3(in_4), .out_4(mux2_1_out_4));
  MUX2 mux2_2 (.in_1(in_1), .in_2(in_5), .in_3(in_6), .out_4(mux2_2_out_4));
  MUX2 mux2_3 (.in_1(in_2), .in_2(mux2_1_out_4), .in_3(mux2_2_out_4), .out_4(out_7));
endmodule

module \ProblèmeCafé  (
  input  \Café ,
  input  Sucre,
  input  Bouillon
);

  wire and_1_out, and_2_out, and_3_out, and_4_out, and_5_out, not_1_out, or_1_out, or_2_out;

  and and_1 (and_1_out, Sucre, \Café );
  and and_2 (and_2_out, \Café , Bouillon);
  and and_3 (and_3_out, Sucre, Bouillon);
  and and_4 (and_4_out, \Café , Sucre, Bouillon);
  or or_1 (or_1_out, and_2_out, Sucre, and_3_out);
  not not_1 (not_1_out, and_1_out);
  and and_5 (and_5_out, not_1_out, or_1_out);
  or or_2 (or_2_out, and_5_out, and_4_out);
  LED led_1 (.in(or_2_out));
endmodule

module \ProblèmeCafé_Antocad  (
  input  Sucre,
  input  Cafe,
  input  Bouillon,
  output out_4
);

  wire and_1_out, and_2_out, and_3_out, mon_xor_1_out_3, not_1_out, not_2_out, or_1_out, or_2_out;

  and and_1 (and_1_out, Sucre, Cafe);
  not not_1 (not_1_out, Sucre);
  or or_1 (or_1_out, and_1_out, Cafe);
  and and_2 (and_2_out, not_1_out, Bouillon);
  and and_3 (and_3_out, or_1_out, Bouillon);
  not not_2 (not_2_out, mon_xor_1_out_3);
  mon_xor mon_xor_1 (.a(or_1_out), .b(and_2_out), .out_3(mon_xor_1_out_3));
  or or_2 (or_2_out, not_2_out, and_3_out);
  LED led_1 (.in(or_2_out));
  not not_3 (out_4, or_2_out);
endmodule
