// Logisim project TME2.circ as structural Verilog: 6 circuits, main circuit ex1q1
module ex1q1 (
  input  a,
  input  b,
  input  cin,
  output s,
  output cout
);

  wire and_1_out, and_2_out, and_3_out, and_4_out, and_5_out, and_6_out, and_7_out, not_1_out, not_2_out,
       not_3_out;

  not not_1 (not_1_out, a);
  not not_2 (not_2_out, b);
  not not_3 (not_3_out, cin);
  and and_1 (and_1_out, not_1_out, not_2_out, cin);
  and and_2 (and_2_out, not_1_out, b, not_3_out);
  and and_3 (and_3_out, a, not_2_out, not_3_out);
  and and_4 (and_4_out, a, b, cin);
  and and_5 (and_5_out, a, b, not_3_out);
  and and_6 (and_6_out, a, not_2_out, cin);
  and and_7 (and_7_out, not_1_out, b, cin);
  or or_1 (s, and_1_out, and_2_out, and_3_out, and_4_out);
  or or_2 (cout, and_4_out, and_5_out, and_6_out, and_7_out);
endmodule

module ex1q2 (
  input  a,
  input  b,
  input  cin,
  output s,
  output cout
);

  wire and_1_out, and_2_out, xor_1_out, xor_2_out;

  xor xor_1 (xor_1_out, a, b);
  and and_1 (and_1_out, a, b);
  xor xor_2 (xor_2_out, a, b);
  and and_2 (and_2_out, xor_2_out, cin);
  xor xor_3 (s, xor_1_out, cin);
  or or_1 (cout, and_1_out, and_2_out);
endmodule

module ex1q3 (
  input  cin,
  input  a0,
  input  a1,
  input  a2,
  input  a3,
  input  b0,
  input  b1,
  input  b2,
  input  b3,
  output s0,
  output s1,
  output s2,
  output s3,
  output cout
);

  wire ex1q2_1_cout, ex1q2_2_cout, ex1q2_3_cout;

  ex1q2 ex1q2_1 (.a(a0), .b(b0), .cin(cin), .s(s0), .cout(ex1q2_1_cout));
  ex1q2 ex1q2_2 (.a(a1), .b(b1), .cin(ex1q2_1_cout), .s(s1), .cout(ex1q2_2_cout));
  ex1q2 ex1q2_3 (.a(a2), .b(b2), .cin(ex1q2_2_cout), .s(s2), .cout(ex1q2_3_cout));
  ex1q2 ex1q2_4 (.a(a3), .b(b3), .cin(ex1q2_3_cout), .s(s3), .cout(cout));
endmodule

module ex2q3 (
  input  a,
  input  b,
  input  bin,
  output d,
  output bout
);

  wire and_1_out, and_2_out, and_3_out, and_4_out, and_5_out, not_1_out, not_2_out, not_3_out, not_4_out,
       or_1_out, xor_1_out, xor_2_out;

  not not_1 (not_1_out, bin);
  not not_2 (not_2_out, a);
  xor xor_1 (xor_1_out, a, b);
  not not_3 (not_3_out, a);
  xor xor_2 (xor_2_out, a, b);
  and and_1 (and_1_out, not_2_out, b);
  not not_4 (not_4_out, xor_1_out);
  or or_1 (or_1_out, not_4_out, and_2_out);
  and and_2 (and_2_out, not_3_out, b);
  and and_3 (and_3_out, not_1_out, xor_2_out);
  and and_4 (and_4_out, not_1_out, and_1_out);
  and and_5 (and_5_out, or_1_out, bin);
  or or_2 (d, and_5_out, and_3_out);
  or or_3 (bout, and_5_out, and_4_out);
endmodule

module ex2q4 (
  input  bin,
  input  a0,
  input  a1,
  input  a2,
  input  a3,
  input  b0,
  input  b1,
  input  b2,
  input  b3,
  output d0,
  output d1,
  output d2,
  output d3,
  output Bout
);

  wire ex2q3_1_bout, ex2q3_2_bout, ex2q3_3_bout;

  ex2q3 ex2q3_1 (.a(a0), .b(b0), .bin(bin), .d(d0), .bout(ex2q3_1_bout));
  ex2q3 ex2q3_2 (.a(a1), .b(b1), .bin(ex2q3_1_bout), .d(d1), .bout(ex2q3_2_bout));
  ex2q3 ex2q3_3 (.a(a2), .b(b2), .bin(ex2q3_2_bout), .d(d2), .bout(ex2q3_3_bout));
  ex2q3 ex2q3_4 (.a(a3), .b(b3), .bin(ex2q3_3_bout), .d(d3), .bout(Bout));
endmodule

module ex3q1 (
  input  [3:0] a,
  input  [3:0] b,
  input  CY,
  input  Add_Sub,
  output [3:0] s,
  output Out
);

  wire ex1q3_1_cout, ex2q4_1_bout;
  wire [3:0] ex1q3_1_s0, ex2q4_1_d0;

  ex1q3 ex1q3_1 (
    .cin(CY), .a0(a[0]), .a1(a[1]), .a2(a[2]), .a3(a[3]), .b0(b[0]), .b1(b[1]), .b2(b[2]), .b3(b[3]),
    .s0(ex1q3_1_s0[0]), .s1(ex1q3_1_s0[1]), .s2(ex1q3_1_s0[2]), .s3(ex1q3_1_s0[3]), .cout(ex1q3_1_cout));
  ex2q4 ex2q4_1 (
    .bin(CY), .a0(a[0]), .a1(a[1]), .a2(a[2]), .a3(a[3]), .b0(b[0]), .b1(b[1]), .b2(b[2]), .b3(b[3]),
    .d0(ex2q4_1_d0[0]), .d1(ex2q4_1_d0[1]), .d2(ex2q4_1_d0[2]), .d3(ex2q4_1_d0[3]), .Bout(ex2q4_1_bout));
  Multiplexer #(.width(4)) multiplexer_1 (.in0(ex1q3_1_s0), .in1(ex2q4_1_d0), .out(s), .sel(Add_Sub));  // open: en
  Multiplexer multiplexer_2 (.in0(ex1q3_1_cout), .in1(ex2q4_1_bout), .out(Out), .sel(Add_Sub));  // open: en
endmodule
