// Logisim project TME3.circ as structural Verilog: 8 circuits, main circuit additionneur4bits
module additionneur4bits (
  input  cin,
  input  a0,
  input  a1,
  input  a2,
  input  a3,
  input  b0,
  input  b1,
  input  b2,
  input  b3,
  output s0,
  output s1,
  output s2,
  output s3,
  output cout
);

  wire additionneur1bit_1_cout, additionneur1bit_2_cout, additionneur1bit_3_cout;

  additionneur1bit additionneur1bit_1 (.a(a0), .b(b0), .cin(cin), .s(s0), .cout(additionneur1bit_1_cout));
  additionneur1bit additionneur1bit_2 (
    .a(a1), .b(b1), .cin(additionneur1bit_1_cout), .s(s1), .cout(additionneur1bit_2_cout));
  additionneur1bit additionneur1bit_3 (
    .a(a2), .b(b2), .cin(additionneur1bit_2_cout), .s(s2), .cout(additionneur1bit_3_cout));
  additionneur1bit additionneur1bit_4 (.a(a3), .b(b3), .cin(additionneur1bit_3_cout), .s(s3), .cout(cout));
endmodule

module soustracteur4bits (
  input  bin,
  input  a0,
  input  a1,
  input  a2,
  input  a3,
  input  b0,
  input  b1,
  input  b2,
  input  b3,
  output d0,
  output d1,
  output d2,
  output d3,
  output Bout
);

  wire soustracteur1bit_1_bout, soustracteur1bit_2_bout, soustracteur1bit_3_bout;

  soustracteur1bit soustracteur1bit_1 (.a(a0), .b(b0), .bin(bin), .d(d0), .bout(soustracteur1bit_1_bout));
  soustracteur1bit soustracteur1bit_2 (
    .a(a1), .b(b1), .bin(soustracteur1bit_1_bout), .d(d1), .bout(soustracteur1bit_2_bout));
  soustracteur1bit soustracteur1bit_3 (
    .a(a2), .b(b2), .bin(soustracteur1bit_2_bout), .d(d2), .bout(soustracteur1bit_3_bout));
  soustracteur1bit soustracteur1bit_4 (.a(a3), .b(b3), .bin(soustracteur1bit_3_bout), .d(d3), .bout(Bout));
endmodule

module additionneur1bit (
  input  a,
  input  b,
  input  cin,
  output s,
  output cout
);

  wire and_1_out, and_2_out, and_3_out, xor_1_out;

  and and_1 (and_1_out, a, b);
  and and_2 (and_2_out, a, cin);
  and and_3 (and_3_out, b, cin);
  xor xor_1 (xor_1_out, a, b);
  xor xor_2 (s, xor_1_out, cin);
  or or_1 (cout, and_1_out, and_2_out, and_3_out);
endmodule

module soustracteur1bit (
  input  a,
  input  b,
  input  bin,
  output d,
  output bout
);

  wire and_1_out, and_2_out, and_3_out, and_4_out, and_5_out, not_1_out, not_2_out, not_3_out, not_4_out,
       or_1_out, xor_1_out, xor_2_out;

  not not_1 (not_1_out, bin);
  not not_2 (not_2_out, a);
  xor xor_1 (xor_1_out, a, b);
  not not_3 (not_3_out, a);
  xor xor_2 (xor_2_out, a, b);
  and and_1 (and_1_out, not_2_out, b);
  not not_4 (not_4_out, xor_1_out);
  or or_1 (or_1_out, not_4_out, and_2_out);
  and and_2 (and_2_out, not_3_out, b);
  and and_3 (and_3_out, not_1_out, xor_2_out);
  and and_4 (and_4_out, not_1_out, and_1_out);
  and and_5 (and_5_out, or_1_out, bin);
  or or_2 (d, and_5_out, and_3_out);
  or or_3 (bout, and_5_out, and_4_out);
endmodule

module ex1 (
  input  [3:0] X,
  input  [3:0] Y,
  input  Aluop,
  output [3:0] out_4,
  output OV,
  output ZF,
  output SF,
  output CF
);

  wire not_2_out, or_1_out;
  wire [3:0] multiplexer_1_out, not_1_out;

  assign not_1_out = ~Y;  // NOT_Gate not_1, 4 bits wide
  Multiplexer #(.width(4)) multiplexer_1 (.in0(Y), .in1(not_1_out), .out(multiplexer_1_out), .sel(Aluop));  // open: en
  additionneur4bits additionneur4bits_1 (
    .cin(Aluop), .a0(X[0]), .a1(X[1]), .a2(X[2]), .a3(X[3]), .b0(multiplexer_1_out[0]),
    .b1(multiplexer_1_out[1]), .b2(multiplexer_1_out[2]), .b3(multiplexer_1_out[3]), .s0(out_4[0]),
    .s1(out_4[1]), .s2(out_4[2]), .s3(out_4[3]), .cout(CF));
  Multiplexer multiplexer_2 (.in0(CF), .in1(not_2_out), .out(OV), .sel(Aluop));  // open: en
  not not_2 (not_2_out, CF);
  or or_1 (or_1_out, out_4[0], out_4[1], out_4[2], out_4[3], OV);
  xor xor_1 (SF, CF, Aluop);
  not not_3 (ZF, or_1_out);
endmodule

module ex2 (
  input  [3:0] A,
  input  [1:0] D,
  output [3:0] S
);

  Multiplexer #(.select(2), .width(4)) multiplexer_1 (
    .in0(A), .in1({1'b0, A[3:1]}), .in2({2'b00, A[3:2]}), .in3({3'b000, A[3]}), .out(S), .sel(D));  // open: en
endmodule

module ex3 (
  input  [3:0] A,
  input  [1:0] D,
  output [3:0] S
);

  wire [0:0] not_1_out;
  wire [1:0] not_2_out;
  wire [2:0] not_4_out;

  not not_1 (not_1_out[0], 1'b1);
  not not_2 (not_2_out[0], 1'b1);
  not not_3 (not_2_out[1], 1'b1);
  not not_4 (not_4_out[0], 1'b1);
  not not_5 (not_4_out[1], 1'b1);
  not not_6 (not_4_out[2], 1'b1);
  Multiplexer #(.select(2), .width(4)) multiplexer_1 (
    .in0(A), .in1({A[2:0], not_1_out[0]}), .in2({A[1:0], not_2_out}), .in3({A[0], not_4_out}), .out(S),
    .sel(D));  // open: en
endmodule

module ex4 (
  input  [3:0] A,
  input  [3:0] B,
  input  [3:0] A_2,
  input  [3:0] B_2
);

  wire and_1_out, nand_1_out, or_1_out, soustracteur4bits_1_bout, soustracteur4bits_2_bout,
       soustracteur4bits_2_d0, soustracteur4bits_2_d1, soustracteur4bits_2_d2, soustracteur4bits_2_d3;

  soustracteur4bits soustracteur4bits_1 (
    .bin(1'b0), .a0(A_2[0]), .a1(A_2[1]), .a2(A_2[2]), .a3(A_2[3]), .b0(B_2[0]), .b1(B_2[1]), .b2(B_2[2]),
    .b3(B_2[3]), .Bout(soustracteur4bits_1_bout));  // open: d0, d1, d2, d3
  soustracteur4bits soustracteur4bits_2 (
    .bin(1'b0), .a0(B[0]), .a1(B[1]), .a2(B[2]), .a3(B[3]), .b0(A[0]), .b1(A[1]), .b2(A[2]), .b3(A[3]),
    .d0(soustracteur4bits_2_d0), .d1(soustracteur4bits_2_d1), .d2(soustracteur4bits_2_d2),
    .d3(soustracteur4bits_2_d3), .Bout(soustracteur4bits_2_bout));
  LED B___A (.in(soustracteur4bits_1_bout));
  or or_1 (or_1_out, soustracteur4bits_2_d0, soustracteur4bits_2_d1, soustracteur4bits_2_d2, soustracteur4bits_2_d3);
  nand nand_1 (nand_1_out, or_1_out, soustracteur4bits_2_bout);
  and and_1 (and_1_out, or_1_out, nand_1_out);
  LED B___A_2 (.in(and_1_out));

  // Notes on the sheet:
  //   Ou
endmodule
