// Logisim project TME4.circ as structural Verilog: 7 circuits, main circuit main
module additionneur1bit (
  input  a,
  input  b,
  input  cin,
  output s,
  output cout
);

  wire and_1_out, and_2_out, and_3_out, xor_1_out;

  and and_1 (and_1_out, a, b);
  and and_2 (and_2_out, a, cin);
  and and_3 (and_3_out, b, cin);
  xor xor_1 (xor_1_out, a, b);
  xor xor_2 (s, xor_1_out, cin);
  or or_1 (cout, and_1_out, and_2_out, and_3_out);
endmodule

module additionneur4bits (
  input  cin,
  input  a0,
  input  a1,
  input  a2,
  input  a3,
  input  b0,
  input  b1,
  input  b2,
  input  b3,
  output s0,
  output s1,
  output s2,
  output s3,
  output cout
);

  wire additionneur1bit_1_cout, additionneur1bit_2_cout, additionneur1bit_3_cout;

  additionneur1bit additionneur1bit_1 (.a(a0), .b(b0), .cin(cin), .s(s0), .cout(additionneur1bit_1_cout));
  additionneur1bit additionneur1bit_2 (
    .a(a1), .b(b1), .cin(additionneur1bit_1_cout), .s(s1), .cout(additionneur1bit_2_cout));
  additionneur1bit additionneur1bit_3 (
    .a(a2), .b(b2), .cin(additionneur1bit_2_cout), .s(s2), .cout(additionneur1bit_3_cout));
  additionneur1bit additionneur1bit_4 (.a(a3), .b(b3), .cin(additionneur1bit_3_cout), .s(s3), .cout(cout));
endmodule

module ALU (
  input  [3:0] X,
  input  [3:0] Y,
  input  Aluop,
  output [3:0] out_4,
  output OV,
  output ZF,
  output SF,
  output CF
);

  wire not_2_out, or_1_out;
  wire [3:0] multiplexer_1_out, not_1_out;

  assign not_1_out = ~Y;  // NOT_Gate not_1, 4 bits wide
  Multiplexer #(.width(4)) multiplexer_1 (.in0(Y), .in1(not_1_out), .out(multiplexer_1_out), .sel(Aluop));  // open: en
  additionneur4bits additionneur4bits_1 (
    .cin(Aluop), .a0(X[0]), .a1(X[1]), .a2(X[2]), .a3(X[3]), .b0(multiplexer_1_out[0]),
    .b1(multiplexer_1_out[1]), .b2(multiplexer_1_out[2]), .b3(multiplexer_1_out[3]), .s0(out_4[0]),
    .s1(out_4[1]), .s2(out_4[2]), .s3(out_4[3]), .cout(CF));
  Multiplexer multiplexer_2 (.in0(CF), .in1(not_2_out), .out(OV), .sel(Aluop));  // open: en
  not not_2 (not_2_out, CF);
  or or_1 (or_1_out, out_4[0], out_4[1], out_4[2], out_4[3], OV);
  xor xor_1 (SF, CF, Aluop);
  not not_3 (ZF, or_1_out);
endmodule

module main (
  input  [3:0] Din,
  input  WE,
  output [3:0] Dout
);

  wire CK_out;

  Clock CK (.out(CK_out));
  Register #(.width(4)) Register (.D(Din), .en(WE), .Q(Dout), .clk(CK_out), .clr(1'b0));
endmodule

module \Mémoire  (
  input  [3:0] ADRESS_IN,
  input  [7:0] DATA_IN,
  input  [2:0] COMMAND_IN,
  output [7:0] DATA_OUT
);

  wire clock_1_out;

  Clock clock_1 (.out(clock_1_out));
  RAM #(.addrWidth(4), .bus("separate")) ram_1 (
    .addr(ADRESS_IN), .din(DATA_IN), .data(DATA_OUT), .str(COMMAND_IN[0]), .sel(COMMAND_IN[1]),
    .clk(clock_1_out), .ld(COMMAND_IN[2]), .clr(1'b0));
endmodule

module \Mémoire2  (
  input  [7:0] ADRESS_IN,
  input  [31:0] DATA_IN,
  input  [2:0] COMMAND_IN,
  output [31:0] DATA_OUT
);

  wire clock_1_out;

  Clock clock_1 (.out(clock_1_out));
  RAM #(.dataWidth(32), .bus("separate")) ram_1 (
    .addr(ADRESS_IN), .din(DATA_IN), .data(DATA_OUT), .str(COMMAND_IN[0]), .sel(COMMAND_IN[1]),
    .clk(clock_1_out), .ld(COMMAND_IN[2]), .clr(1'b0));
endmodule

module RegistresAlu (
  input  [3:0] Din,
  input  ext_A,
  input  WE_A,
  input  [3:0] Din_2,
  input  ext_B,
  input  WE_B,
  input  [3:0] Din_3,
  input  ext_C,
  input  WE_C,
  input  [3:0] Din_4,
  input  ext_D,
  input  WE_D,
  input  Add_Subb,
  input  [1:0] OP_X,
  input  [1:0] OP_Y,
  output CF,
  output OV,
  output SF,
  output ZF
);

  wire clock_1_out;
  wire [3:0] alu_1_out_4, multiplexer_1_out, multiplexer_2_out, multiplexer_3_out, multiplexer_4_out,
       multiplexer_5_out, multiplexer_6_out, RA_q, RB_q, undriven;

  Register #(.width(4)) RA (.D(multiplexer_1_out), .en(WE_A), .Q(RA_q), .clk(clock_1_out));  // open: clr
  Multiplexer #(.width(4)) multiplexer_1 (
    .in0(alu_1_out_4), .in1(Din), .out(multiplexer_1_out), .sel(ext_A));  // open: en
  Register #(.width(4)) RB (.D(multiplexer_2_out), .en(WE_B), .Q(RB_q), .clk(clock_1_out));  // open: clr
  Multiplexer #(.width(4)) multiplexer_2 (
    .in0(alu_1_out_4), .in1(Din_2), .out(multiplexer_2_out), .sel(ext_B));  // open: en
  Register #(.width(4)) RC (.D(multiplexer_3_out), .clk(clock_1_out));  // open: en, Q, clr
  Multiplexer #(.width(4)) multiplexer_3 (
    .in0(alu_1_out_4), .in1(Din_3), .out(multiplexer_3_out), .sel(ext_C));  // open: en
  Multiplexer #(.width(4)) multiplexer_4 (
    .in0(alu_1_out_4), .in1(Din_4), .out(multiplexer_4_out), .sel(ext_D));  // open: en
  Register #(.width(4)) RD (.D(multiplexer_4_out), .Q(RA_q), .clk(clock_1_out));  // open: en, clr
  Clock clock_1 (.out(clock_1_out));
  Multiplexer #(.select(2), .width(4)) multiplexer_5 (
    .in0(RA_q), .in1(RA_q), .in2(RB_q), .in3(undriven), .out(multiplexer_5_out), .sel(OP_X));  // open: en
  Multiplexer #(.select(2), .width(4)) multiplexer_6 (
    .in0(RA_q), .in1(RA_q), .in2(RB_q), .in3(undriven), .out(multiplexer_6_out), .sel(OP_Y));  // open: en
  ALU alu_1 (
    .X(multiplexer_5_out), .Y(multiplexer_6_out), .Aluop(Add_Subb), .out_4(alu_1_out_4), .OV(OV), .ZF(ZF),
    .SF(SF), .CF(CF));
endmodule
